# Fritzing sketch blueAndLed (saved by Fritzing 0.9.0b)

parts:
  Parte1 = Bluetooth HC-05 Macho
  Parte2 = Arduino Mega 2560 (Rev3)

nets:
  N1: Parte1.TXD, Parte2.D2_PWM
  N2: Parte1.RXD, Parte2.D3_PWM
  VCC: Parte1.VCC, Parte2.3V3
  GND: Parte1.GND, Parte2.GND

notes:
  TXD a pin 2 del arduino y RXD a pin 3
  Tierra y voltaje
  Desde el blueterm en el celular, al precionar 1 prendia el led 13 que tiene incluido el arduino y viceversa si precionabas 0
  La conexion muy sencilla pero podemos notar las grandes ventajas que nos ofrece el uso del modulo bluetooth y librerias ya hechas para arduinos como la <SoftwareSerial.h> sin dejar atras a BlueTerm que nos da una muy facil conexion a nuestro modulo
